# Fritzing sketch 1master_1slave (saved by Fritzing 0.9.3b)
breadboards: 1

parts:
  DHT1 = Humidity and Temperature Sensor DHT11
  Part1 = Arduino Nano (Rev3.0)
  Part2 = Arduino Uno (Rev3)
  U1 = POT [package=pot_mammoth]
  R1 = Resistor [tolerance=±5% resistance=6.8k package="1206 [SMD]"]
  R2 = Resistor [tolerance=±5% resistance=4.7k package="1206 [SMD]"]
  R3 = Resistor [tolerance=±5% resistance=4.7k package="1206 [SMD]"]

nets:
  5V: DHT1.Vcc, Part1.5V, Part2.5V, U1.S, R1.Pin_1, R2.Pin_0, R3.Pin_0
  N1: DHT1.Data-signal, Part1.D7, R1.Pin_0
  GND: DHT1.GND_2, Part1.GND, Part2.GND, U1.E
  N2: Part1.A5, Part2.A5/SCL, R2.Pin_1
  N3: Part1.A4, Part2.A4/SDA, R3.Pin_1
  N4: Part1.A0, U1.A

custom parts:
  Humidity and Temperature Sensor DHT11: Digital relative humidity & temperature sensor DHT11
