# Fritzing sketch 1master_3slaves (saved by Fritzing 0.9.3b)
breadboards: 3

parts:
  Autor_Ignacio_De_Bonis = Humidity and Temperature Sensor DHT11
  U1 = POT [package=pot_mammoth]
  R1 = Resistor [tolerance=±5% resistance=6.8k package="1206 [SMD]"]
  R2 = Resistor [tolerance=±5% resistance=4.7k package="1206 [SMD]"]
  R3 = Resistor [tolerance=±5% resistance=4.7k package="1206 [SMD]"]
  RTC_module = ZS-042 RTC Module
  Master = Arduino Uno (Rev3)
  Fecha_26_de_Mayo_2021 = Humidity and Temperature Sensor DHT11
  Slave_2 = Arduino Nano (Rev3.0)
  U2 = POT [package=pot_mammoth]
  R4 = Resistor [tolerance=±5% resistance=6.8k package="1206 [SMD]"]
  Slave_1 = Arduino Nano (Rev3.0)

nets:
  5V: Autor_Ignacio_De_Bonis.Vcc, U1.S, R1.Pin_1, R2.Pin_0, R3.Pin_0, RTC_module.VCC, Master.5V, Fecha_26_de_Mayo_2021.Vcc, Slave_2.5V, U2.S, R4.Pin_1, Slave_1.5V
  N1: Autor_Ignacio_De_Bonis.Data-signal, R1.Pin_0, Slave_1.D7
  GND: Autor_Ignacio_De_Bonis.GND_2, U1.E, RTC_module.GND, Master.GND, Fecha_26_de_Mayo_2021.GND_2, Slave_2.GND, U2.E, Slave_1.GND
  N2: U1.A, Slave_1.A0
  SDA: R2.Pin_1, RTC_module.SDA, Master.A4/SDA, Slave_2.A4, Slave_1.A4
  SCL: R3.Pin_1, RTC_module.SCL, Master.A5/SCL, Slave_2.A5, Slave_1.A5
  Vin: Master.VIN, Slave_2.VIN, Slave_1.VIN
  N3: Fecha_26_de_Mayo_2021.Data-signal, Slave_2.D7, R4.Pin_0
  N4: Slave_2.A0, U2.A

custom parts:
  Humidity and Temperature Sensor DHT11: Digital relative humidity & temperature sensor DHT11
